// Logisim project alu.circ as structural Verilog: 1 circuit, main circuit myALU
module myALU (
  input  [31:0] Input1,
  input  [31:0] Input2,
  input  [3:0] op,
  output zero,
  output [31:0] Result
);

  wire comparator_1_eq, comparator_1_gt, comparator_1_lt, not_1_out, or_2_out, or_3_out;
  wire [31:0] adder_1_out, and_1_out, bit_extender_1_out, bit_extender_2_out, bit_extender_3_out,
       bit_extender_4_out, bit_extender_5_out, bit_extender_6_out, divider_1_out, multiplier_1_out,
       nor_1_out, or_1_out, shifter_1_out, shifter_2_out, subtractor_1_out, xor_1_out;

  Adder #(.width(32)) adder_1 (.a(Input1), .b(Input2), .out(adder_1_out));  // open: cin, cout
  Subtractor #(.width(32)) subtractor_1 (.a(Input1), .b(Input2), .out(subtractor_1_out));  // open: bin, bout
  Multiplier #(.width(32)) multiplier_1 (.a(Input1), .b(Input2), .out(multiplier_1_out));  // open: cin, cout
  Divider #(.width(32)) divider_1 (.a(Input1), .b(Input2), .out(divider_1_out));  // open: upper, rem
  Shifter #(.width(32)) shifter_1 (.in(Input1), .\dist (Input2[4:0]), .out(shifter_1_out));
  Shifter #(.shift("lr"), .width(32)) shifter_2 (.in(Input1), .\dist (Input2[4:0]), .out(shifter_2_out));
  Shifter #(.shift("ar"), .width(32)) shifter_3 (.in(Input1), .\dist (Input2[4:0]));  // open: out
  assign or_1_out = Input1 | Input2;  // OR_Gate or_1, 32 bits wide
  assign and_1_out = Input1 & Input2;  // AND_Gate and_1, 32 bits wide
  assign xor_1_out = Input1 ^ Input2;  // XOR_Gate xor_1, 32 bits wide
  assign nor_1_out = ~(Input1 | Input2);  // NOR_Gate nor_1, 32 bits wide
  Comparator #(.width(32)) comparator_1 (
    .a(Input1), .b(Input2), .gt(comparator_1_gt), .eq(comparator_1_eq), .lt(comparator_1_lt));
  not not_1 (not_1_out, comparator_1_eq);
  assign bit_extender_1_out = {{31{1'b0}}, comparator_1_gt};  // Bit_Extender bit_extender_1
  assign bit_extender_2_out = {{31{1'b0}}, or_2_out};  // Bit_Extender bit_extender_2
  or or_2 (or_2_out, comparator_1_gt, comparator_1_eq);
  assign bit_extender_3_out = {{31{1'b0}}, comparator_1_eq};  // Bit_Extender bit_extender_3
  assign bit_extender_4_out = {{31{1'b0}}, not_1_out};  // Bit_Extender bit_extender_4
  assign bit_extender_5_out = {{31{1'b0}}, or_3_out};  // Bit_Extender bit_extender_5
  or or_3 (or_3_out, comparator_1_eq, comparator_1_lt);
  assign bit_extender_6_out = {{31{1'b0}}, comparator_1_lt};  // Bit_Extender bit_extender_6
  Multiplexer #(.select(4), .width(32)) multiplexer_1 ();  // open: in0, in1, in2, in3, in4, in5, in6, in7, in8, in9, in10, in11, in12, in13, in14, in15, out, sel
  Comparator #(.width(32)) comparator_2 (.a({32{1'b0}}), .b(Result), .eq(zero));  // open: gt, lt

  // Other names for the same wires on the sheet: in1[31:0] = Input1; in2[31:0] = Input2; res[31:0] = Result

  // Notes on the sheet:
  //   Inputs
  //   Outputs
endmodule
