// Logisim project control_unit.circ as structural Verilog: 1 circuit, main circuit control_unit
module control_unit (
  input  [5:0] opcode,
  input  [5:0] func,
  output Reg_Write,
  output ALU_Src,
  output [1:0] PC_control,
  output [1:0] Reg_Dest_Sel,
  output [1:0] Reg_Write_Sel,
  output [1:0] MEMW_Sel
);

  PLA #(.in_width(12), .out_width(10), .\table ("xxxxxx001000 0000000011 # ADDi\nxxxxxx001001 0000000011 # ADDiu\nxxxxxx001100 0000000011 # ANDi\nxxxxxx001110 0000000011 # XORi\nxxxxxx001101 0000000011 # ORi\nxxxxxx000100 0000000110 # BEQ\nxxxxxx000101 0000000110 # BNE\nxxxxxx000110 0000000110 # BLEZ\nxxxxxx000111 0000000110 # BGTZ\nxxxxxx000001 0000000110 # BGEZ\nxxxxxx100011 0001000011 # LW\nxxxxxx101011 0100000010 # SW\nxxxxxx100000 0001000011 # LB\nxxxxxx101000 1000000010 # SB\nxxxxxx001010 0000000011 # SLTi\nxxxxxx001111 0000000011 # Lui\nxxxxxx000010 0000001000 # J\nxxxxxx000011 0010101000 # JAL\n100110000000 0000010001 # XOR\n000000000000 0000010001 # SLL\n000100000000 0000010001 # SLLV\n000010000000 0000010001 # SRL\n100010000000 0000010001 # SUB\n000110000000 0000010001 # SRLV\n101010000000 0000010001 # SLT\n001100000000 0000000000 # Syscall\n100011000000 0000010001 # SUBu\n100101000000 0000010001 # OR\n100111000000 0000010001 # NOR\n100001000000 0000010001 # ADDu\n011000000000 0000010001 # MULT\n011010000000 0000010001 # DIV\n100100000000 0000010001 # AND\n100000000000 0000010001 # ADD\n001000000000 0000001100 # JR\n000011000000 0000010001 # SRA")) Program_Scheduler (
    .in({opcode, func}), .out({MEMW_Sel, Reg_Write_Sel, Reg_Dest_Sel, PC_control, ALU_Src, Reg_Write}));

  // Other names for the same wires on the sheet: MEMW_Mask_Sel[1:0] = MEMW_Sel

  // Notes on the sheet:
  //   Input
  //   done
  //   Outputs
  //   done
  //   done
  //   done
  //   PLU_Logic
  //   done
  //   done
endmodule
