// Logisim project cpu.circ as structural Verilog: 1 circuit, main circuit cpu
module cpu (
  output [31:0] out_1,
  output [31:0] out_2,
  output out_3,
  output out_4,
  output out_5,
  output [5:0] out_6,
  output out_7,
  output out_8
);

  wire ALU_Src_EX, ALU_Src_ID, ALU_Src_MEM, ALU_Src_WB, and_1_out, and_2_out, and_3_out,
       cache_1_wb_mask_select, Finish_EX, Finish_ID, Finish_MEM, Finish_WB, hit_MEM, hit_WB,
       is_branch_inst_IF, is_JR_inst_IF, is_jump_inst_IF, is_mem_inst_EX, is_mem_inst_ID, is_mem_inst_MEM,
       is_mem_inst_WB, mem_fetch_done, mem_mask_sel, not_1_out, not_2_out, not_3_out, not_4_out, not_5_out,
       not_6_out, or_1_out, Reg_Write_EX, Reg_Write_ID, Reg_Write_MEM, Reg_Write_WB, Zero_EX;
  wire [1:0] mem_data_sel, MEMW_Sel_EX, MEMW_Sel_ID, MEMW_Sel_MEM, MEMW_Sel_WB, PC_control_EX, PC_control_ID,
       PC_control_MEM, PC_control_WB, Reg_Dest_EX, Reg_Dest_ID, Reg_Dest_MEM, Reg_Dest_WB, Reg_Write_Sel_EX,
       Reg_Write_Sel_ID, Reg_Write_Sel_MEM, Reg_Write_Sel_WB, Shift_Select;
  wire [2:0] mem_addr_sel;
  wire [3:0] decoder_1_out0, multiplexer_7_out, multiplexer_9_out;
  wire [4:0] ALU_Ctrl, multiplexer_4_out, multiplexer_6_out, rd_EX, rd_ID, rd_MEM, rd_WB, rs_EX, rs_ID,
       rs_MEM, rs_WB, rt_EX, rt_ID, rt_MEM, rt_WB, SHA_EX, SHA_ID, SHA_MEM, SHA_WB;
  wire [5:0] Func_EX, Func_ID, Func_IF, Func_MEM, Func_WB, opcode_EX, opcode_ID, opcode_IF, opcode_MEM,
       opcode_WB;
  wire [7:0] miss_counter_state;
  wire [25:6] J_addr;
  wire [31:0] ALU_Result_EX, ALU_Result_MEM, ALU_Result_WB, cache_1_fetch0_addr, cache_1_fetch1_addr,
       cache_1_fetch2_addr, cache_1_fetch3_addr, cache_1_write_back0_addr, cache_1_write_back0_data,
       cache_1_write_back1_addr, cache_1_write_back1_data, cache_1_write_back2_addr,
       cache_1_write_back2_data, cache_1_write_back3_addr, cache_1_write_back3_data, Imm_ext_EX, Imm_ext_ID,
       Imm_ext_IF, Imm_ext_MEM, Imm_ext_WB, J_value, MemReadData_MEM, MemReadData_WB, multiplexer_3_out,
       multiplexer_5_out, multiplexer_8_out, multiplexer_10_out, newPC, PC_4_IF, PC_4_Imm_IF, PC_EX, PC_ID,
       PC_IF, PC_MEM, PC_q, PC_WB, Read_Data1_EX, Read_Data1_ID, Read_Data1_MEM, Read_Data1_WB,
       Read_Data2_EX, Read_Data2_ID, Read_Data2_MEM, Read_Data2_WB, shifter_1_out;

  not not_1 (not_1_out, Finish_ID);
  not not_2 (not_2_out, out_5);
  Register #(.width(32)) PC (.D(newPC), .en(not_1_out), .clk(not_2_out), .Q(PC_q));  // open: clr
  Clock clock_1 (.out(out_4));
  Register #(.width(32)) register_1 (.D(PC_q), .en(1'b1), .clk(out_4), .Q(PC_IF));  // open: clr
  Counter #(.max('h3), .width(2)) counter_1 ();  // open: clr, load, up, count, clk, D, carry, Q
  and and_1 (and_1_out, out_4, hit_MEM);
  Shifter #(.width(32)) shifter_1 (.in(Imm_ext_IF), .\dist (5'b00010), .out(shifter_1_out));
  PLA #(.in_width(12), .out_width(3), .\table ("xxxxxx001000 000 # ADDi\nxxxxxx001001 000 # ADDiu\nxxxxxx001100 000 # ANDi\nxxxxxx001110 000 # XORi\nxxxxxx001101 000 # ORi\nxxxxxx000100 010 # BEQ\nxxxxxx000101 010 # BNE\nxxxxxx000110 010 # BLEZ\nxxxxxx000111 010 # BGTZ\nxxxxxx000001 010 # BGEZ\nxxxxxx100011 000 # LW\nxxxxxx101011 000 # SW\nxxxxxx100000 001 # LB\nxxxxxx101000 000 # SB\nxxxxxx001010 000 # SLTi\nxxxxxx001111 000 # Lui\nxxxxxx000010 001 # J\nxxxxxx000011 001 # JAL\n100110000000 000 # XOR\n000000000000 000 # SLL\n000100000000 000 # SLLV\n000010000000 000 # SRL\n100010000000 000 # SUB\n000110000000 000 # SRLV\n101010000000 000 # SLT\n001100000000 000 # Syscall\n100011000000 000 # SUBu\n100101000000 000 # OR\n100111000000 000 # NOR\n100001000000 000 # ADDu\n011000000000 000 # MULT\n011010000000 000 # DIV\n100100000000 000 # AND\n100000000000 000 # ADD\n001000000000 100 # JR\n000011000000 000 # SRA")) pla_1 (
    .in({Func_IF, opcode_IF}), .out({is_JR_inst_IF, is_branch_inst_IF, is_jump_inst_IF}));
  Multiplexer #(.width(32)) multiplexer_1 (.in0(PC_4_IF), .in1(J_value), .out(newPC), .sel(is_jump_inst_IF));
  Adder #(.width(32)) adder_1 (.a(PC_IF), .b(32'h4), .out(PC_4_IF));  // open: cin, cout
  Adder #(.width(32)) adder_2 (.a(PC_4_IF), .b(shifter_1_out), .out(PC_4_Imm_IF));  // open: cin, cout
  Shifter #(.width(28)) shifter_2 (.in({2'b00, J_addr, Func_IF}), .\dist (5'b00010), .out(J_value[27:0]));
  Multiplexer multiplexer_2 (.in0(out_4), .in1(and_1_out), .out(out_5), .sel(is_mem_inst_MEM));
  mem InstMem (
    .MemAddress(PC_q), .MemWriteMask(4'b0000), .MemWriteData({32{1'b1}}), .clk(out_5),
    .MemReadData({opcode_IF, J_addr, Func_IF}));
  assign Imm_ext_IF = {{16{J_addr[15]}}, {J_addr[15:6], Func_IF}};  // Bit_Extender bit_extender_1
  Register #(.width(32)) register_2 (.D(PC_IF), .en(1'b1), .clk(out_4), .Q(PC_ID), .clr(or_1_out));
  Register #(.width(6)) register_3 (.D(opcode_IF), .en(1'b1), .clk(out_4), .Q(opcode_ID), .clr(or_1_out));
  Register #(.width(5)) register_4 (.D(J_addr[25:21]), .en(1'b1), .clk(out_4), .Q(rs_ID), .clr(or_1_out));
  Register #(.width(5)) register_5 (.D(J_addr[20:16]), .en(1'b1), .clk(out_4), .Q(rt_ID), .clr(or_1_out));
  Register #(.width(6)) register_6 (.D(Func_IF), .en(1'b1), .clk(out_4), .Q(Func_ID), .clr(or_1_out));
  Register #(.width(5)) register_7 (.D(J_addr[10:6]), .en(1'b1), .clk(out_4), .Q(SHA_ID), .clr(or_1_out));
  Register #(.width(5)) register_8 (.D(J_addr[15:11]), .en(1'b1), .clk(out_4), .Q(rd_ID), .clr(or_1_out));
  Register #(.width(32)) register_9 (.D(Imm_ext_IF), .en(1'b1), .clk(out_4), .Q(Imm_ext_ID), .clr(or_1_out));
  or or_1 (or_1_out, is_branch_inst_IF, is_JR_inst_IF);
  Multiplexer #(.select(2), .width(32)) multiplexer_3 (
    .in0(ALU_Result_WB), .in1(MemReadData_WB), .in2(PC_WB), .in3({{24{1'b0}}, MemReadData_WB[7:0]}),
    .out(multiplexer_3_out), .sel(Reg_Write_Sel_WB));
  PLA #(.in_width(6), .out_width(1), .\table ("100011 1 # LW\n100000 1 # LB\n101000 1 # SB\n101011 1 # SW")) Checker (
    .in(out_6), .out(is_mem_inst_ID));
  Multiplexer #(.select(2), .width(5)) multiplexer_4 (
    .in0(rt_WB), .in1(rd_WB), .in2({5{1'b1}}), .in3(5'b00001), .out(multiplexer_4_out), .sel(Reg_Dest_WB));
  control_unit CU (
    .opcode(opcode_ID), .func(Func_ID), .Reg_Write(Reg_Write_ID), .ALU_Src(ALU_Src_ID),
    .PC_control(PC_control_ID), .Reg_Dest_Sel(Reg_Dest_ID), .Reg_Write_Sel(Reg_Write_Sel_ID),
    .MEMW_Sel(MEMW_Sel_ID), .Finish(Finish_ID));
  // regfile RegisterFile: pin names not known; wires that end beside it: rs_ID, rt_ID, multiplexer_4_out, multiplexer_3_out, Reg_Write_WB, out_5, Read_Data1_ID, Read_Data2_ID
  Register #(.width(32)) register_10 (.D(PC_ID), .en(1'b1), .clk(out_4), .Q(PC_EX));  // open: clr
  Register #(.width(6)) register_11 (.D(opcode_ID), .en(1'b1), .clk(out_4), .Q(opcode_EX));  // open: clr
  Register #(.width(5)) register_12 (.D(rs_ID), .en(1'b1), .clk(out_4), .Q(rs_EX));  // open: clr
  Register #(.width(5)) register_13 (.D(rt_ID), .en(1'b1), .clk(out_4), .Q(rt_EX));  // open: clr
  Register #(.width(6)) register_14 (.D(Func_ID), .en(1'b1), .clk(out_4), .Q(Func_EX));  // open: clr
  Register #(.width(5)) register_15 (.D(SHA_ID), .clk(out_4), .Q(SHA_EX));  // open: en, clr
  Register #(.width(5)) register_16 (.D(rd_ID), .clk(out_4), .Q(rd_EX));  // open: en, clr
  Register #(.width(32)) register_17 (.D(Imm_ext_ID), .en(1'b1), .clk(out_4), .Q(Imm_ext_EX));  // open: clr
  Register #(.width(1)) register_18 (.D(Reg_Write_ID), .en(1'b1), .clk(out_4), .Q(Reg_Write_EX));  // open: clr
  Register #(.width(1)) register_19 (.D(ALU_Src_ID), .en(1'b1), .clk(out_4), .Q(ALU_Src_EX));  // open: clr
  Register #(.width(2)) register_20 (.D(PC_control_ID), .en(1'b1), .clk(out_4), .Q(PC_control_EX));  // open: clr
  Register #(.width(2)) register_21 (.D(Reg_Dest_ID), .en(1'b1), .clk(out_4), .Q(Reg_Dest_EX));  // open: clr
  Register #(.width(2)) register_22 (.D(Reg_Write_Sel_ID), .en(1'b1), .clk(out_4), .Q(Reg_Write_Sel_EX));  // open: clr
  Register #(.width(2)) register_23 (.D(MEMW_Sel_ID), .en(1'b1), .clk(out_4), .Q(MEMW_Sel_EX));  // open: clr
  Register #(.width(1)) register_24 (.D(Finish_ID), .en(1'b1), .clk(out_4), .Q(Finish_EX));  // open: clr
  Register #(.width(32)) register_25 (.D(Read_Data1_ID), .en(1'b1), .clk(out_4), .Q(Read_Data1_EX));  // open: clr
  Register #(.width(32)) register_26 (.D(Read_Data2_ID), .en(1'b1), .clk(out_4), .Q(Read_Data2_EX));  // open: clr
  Register #(.width(1)) register_27 (.D(is_mem_inst_ID), .en(1'b1), .clk(out_4), .Q(is_mem_inst_EX));  // open: clr
  Multiplexer #(.width(32)) multiplexer_5 (
    .in0(Read_Data2_EX), .in1(Imm_ext_EX), .out(multiplexer_5_out), .sel(ALU_Src_EX));
  Multiplexer #(.select(2), .width(5)) multiplexer_6 (
    .in0(SHA_EX), .in1(Read_Data1_EX[4:0]), .in2(5'b10000), .in3({5{1'b0}}), .out(multiplexer_6_out),
    .sel(Shift_Select));
  // alu_control_unit ALU_Control: pin names not known; wires that end beside it: Func_EX, opcode_EX, ALU_Ctrl, Shift_Select
  // ALU ArithLogicUnit: pin names not known; wires that end beside it: Read_Data1_EX, multiplexer_5_out, ALU_Ctrl, multiplexer_6_out, Zero_EX, ALU_Result_EX
  Register #(.width(32)) register_28 (.D(PC_EX), .en(1'b1), .clk(out_4), .Q(PC_MEM));  // open: clr
  Register #(.width(6)) register_29 (.D(opcode_EX), .en(1'b1), .clk(out_4), .Q(opcode_MEM));  // open: clr
  Register #(.width(5)) register_30 (.D(rs_EX), .en(1'b1), .clk(out_4), .Q(rs_MEM));  // open: clr
  Register #(.width(5)) register_31 (.D(rt_EX), .en(1'b1), .clk(out_4), .Q(rt_MEM));  // open: clr
  Register #(.width(6)) register_32 (.D(Func_EX), .en(1'b1), .clk(out_4), .Q(Func_MEM));  // open: clr
  Register #(.width(5)) register_33 (.D(SHA_EX), .en(1'b1), .clk(out_4), .Q(SHA_MEM));  // open: clr
  Register #(.width(5)) register_34 (.D(rd_EX), .en(1'b1), .clk(out_4), .Q(rd_MEM));  // open: clr
  Register #(.width(32)) register_35 (.D(Imm_ext_EX), .en(1'b1), .clk(out_4), .Q(Imm_ext_MEM));  // open: clr
  Register #(.width(1)) register_36 (.D(Reg_Write_EX), .en(1'b1), .clk(out_4), .Q(Reg_Write_MEM));  // open: clr
  Register #(.width(1)) register_37 (.D(ALU_Src_EX), .en(1'b1), .clk(out_4), .Q(ALU_Src_MEM));  // open: clr
  Register #(.width(2)) register_38 (.D(PC_control_EX), .en(1'b1), .clk(out_4), .Q(PC_control_MEM));  // open: clr
  Register #(.width(2)) register_39 (.D(Reg_Dest_EX), .en(1'b1), .clk(out_4), .Q(Reg_Dest_MEM));  // open: clr
  Register #(.width(2)) register_40 (.D(Reg_Write_Sel_EX), .en(1'b1), .clk(out_4), .Q(Reg_Write_Sel_MEM));  // open: clr
  Register #(.width(2)) register_41 (.D(MEMW_Sel_EX), .en(1'b1), .clk(out_4), .Q(MEMW_Sel_MEM));  // open: clr
  Register #(.width(1)) register_42 (.D(Finish_EX), .en(1'b1), .clk(out_4), .Q(Finish_MEM));  // open: clr
  Register #(.width(32)) register_43 (.D(Read_Data1_EX), .en(1'b1), .clk(out_4), .Q(Read_Data1_MEM));  // open: clr
  Register #(.width(32)) register_44 (.D(Read_Data2_EX), .en(1'b1), .clk(out_4), .Q(Read_Data2_MEM));  // open: clr
  Register #(.width(1)) register_45 (.D(is_mem_inst_EX), .en(1'b1), .clk(out_4), .Q(is_mem_inst_MEM));  // open: clr
  Register #(.width(32)) register_46 (.D(ALU_Result_EX), .en(1'b1), .clk(out_4), .Q(ALU_Result_MEM));  // open: clr
  Register #(.width(2)) register_47 (.D(MEMW_Sel_EX), .en(1'b1), .clk(out_4), .Q(MEMW_Sel_MEM));  // open: clr
  Decoder #(.enable("false"), .select(2)) decoder_1 (
    .out0(decoder_1_out0[0]), .out1(decoder_1_out0[1]), .out2(decoder_1_out0[2]), .out3(decoder_1_out0[3]),
    .sel(ALU_Result_MEM[1:0]));
  Multiplexer #(.select(2), .width(4)) multiplexer_7 (
    .in0(4'b0000), .in1(4'b1111), .in2(decoder_1_out0), .in3(4'b0000), .out(multiplexer_7_out),
    .sel(MEMW_Sel_MEM));
  not not_3 (not_3_out, out_4);
  not not_4 (not_4_out, out_4);
  and and_2 (and_2_out, not_3_out, is_mem_inst_MEM);
  Counter #(.max('h12)) counter_2 (
    .clr(hit_MEM), .load(1'b0), .up(1'b1), .clk(and_2_out), .Q(miss_counter_state));  // open: count, D, carry
  Cache cache_1 (
    .memWriteData(Read_Data2_MEM), .memAddress(ALU_Result_MEM), .clk(not_4_out),
    .write_mask(multiplexer_7_out), .miss_counter_state(miss_counter_state), .main_mem_read_data(out_1),
    .is_mem_inst(is_mem_inst_MEM), .hit(hit_MEM), .cacheReadData(MemReadData_MEM),
    .write_back0_addr(cache_1_write_back0_addr), .write_back1_addr(cache_1_write_back1_addr),
    .write_back2_addr(cache_1_write_back2_addr), .write_back3_addr(cache_1_write_back3_addr),
    .fetch0_addr(cache_1_fetch0_addr), .fetch1_addr(cache_1_fetch1_addr), .fetch2_addr(cache_1_fetch2_addr),
    .fetch3_addr(cache_1_fetch3_addr), .write_back0_data(cache_1_write_back0_data),
    .write_back1_data(cache_1_write_back1_data), .write_back2_data(cache_1_write_back2_data),
    .write_back3_data(cache_1_write_back3_data), .wb_mask_select(cache_1_wb_mask_select));
  and and_3 (and_3_out, cache_1_wb_mask_select, mem_mask_sel);
  not not_5 (not_5_out, out_4);
  not not_6 (not_6_out, hit_MEM);
  Multiplexer #(.select(3), .width(32)) multiplexer_8 (
    .in0(cache_1_write_back0_addr), .in1(cache_1_write_back1_addr), .in2(cache_1_write_back2_addr),
    .in3(cache_1_write_back3_addr), .in4(cache_1_fetch0_addr), .in5(cache_1_fetch1_addr),
    .in6(cache_1_fetch2_addr), .in7(cache_1_fetch3_addr), .out(multiplexer_8_out), .sel(mem_addr_sel));
  Multiplexer #(.width(4)) multiplexer_9 (.in0(4'b0000), .in1(4'b1111), .out(multiplexer_9_out), .sel(and_3_out));
  Multiplexer #(.select(2), .width(32)) multiplexer_10 (
    .in0(cache_1_write_back0_data), .in1(cache_1_write_back1_data), .in2(cache_1_write_back2_data),
    .in3(cache_1_write_back3_data), .out(multiplexer_10_out), .sel(mem_data_sel));
  and and_4 (out_8, not_5_out, is_mem_inst_MEM, not_6_out);
  PLA #(.in_width(8), .out_width(7), .\table ("00000000 0001000 # w0_wb_addr\n00000001 0011001 # w1_wb_addr\n00000010 0101010 # w2 wb_addr\n00000011 0111011 # w3_wb_addr\n00000100 0000100 # w0_fetch_addr\n00000101 0000101 # w1_fetch_addr\n00000110 0000110 # w2_fetch_addr\n00000111 0000111 # w3_fetch_addr\n00010001 1000000 # mem_done")) miss_controls (
    .in(miss_counter_state), .out({mem_fetch_done, mem_data_sel, mem_mask_sel, mem_addr_sel}));
  memDelayed memdelayed_1 (
    .MemAddress(multiplexer_8_out), .MemWriteMask(multiplexer_9_out), .MemWriteData(multiplexer_10_out),
    .clk(out_8), .MemReadData(out_1));
  Register #(.width(32)) register_48 (.D(PC_MEM), .en(1'b1), .clk(out_4), .Q(PC_WB));  // open: clr
  Register #(.width(6)) register_49 (.D(opcode_MEM), .en(1'b1), .clk(out_4), .Q(opcode_WB));  // open: clr
  Register #(.width(5)) register_50 (.D(rs_MEM), .en(1'b1), .clk(out_4), .Q(rs_WB));  // open: clr
  Register #(.width(5)) register_51 (.D(rt_MEM), .en(1'b1), .clk(out_4), .Q(rt_WB));  // open: clr
  Register #(.width(6)) register_52 (.D(Func_MEM), .en(1'b1), .clk(out_4), .Q(Func_WB));  // open: clr
  Register #(.width(5)) register_53 (.D(SHA_MEM), .en(1'b1), .clk(out_4), .Q(SHA_WB));  // open: clr
  Register #(.width(5)) register_54 (.D(rd_MEM), .en(1'b1), .clk(out_4), .Q(rd_WB));  // open: clr
  Register #(.width(32)) register_55 (.D(Imm_ext_MEM), .en(1'b1), .clk(out_4), .Q(Imm_ext_WB));  // open: clr
  Register #(.width(1)) register_56 (.D(Reg_Write_MEM), .en(1'b1), .clk(out_4), .Q(Reg_Write_WB));  // open: clr
  Register #(.width(1)) register_57 (.D(ALU_Src_MEM), .en(1'b1), .clk(out_4), .Q(ALU_Src_WB));  // open: clr
  Register #(.width(2)) register_58 (.D(PC_control_MEM), .en(1'b1), .clk(out_4), .Q(PC_control_WB));  // open: clr
  Register #(.width(2)) register_59 (.D(Reg_Dest_MEM), .en(1'b1), .clk(out_4), .Q(Reg_Dest_WB));  // open: clr
  Register #(.width(2)) register_60 (.D(Reg_Write_Sel_MEM), .en(1'b1), .clk(out_4), .Q(Reg_Write_Sel_WB));  // open: clr
  Register #(.width(2)) register_61 (.D(MEMW_Sel_MEM), .en(1'b1), .clk(out_4), .Q(MEMW_Sel_WB));  // open: clr
  Register #(.width(1)) register_62 (.D(Finish_MEM), .en(1'b1), .clk(out_4), .Q(Finish_WB));  // open: clr
  Register #(.width(32)) register_63 (.D(Read_Data1_MEM), .en(1'b1), .clk(out_4), .Q(Read_Data1_WB));  // open: clr
  Register #(.width(32)) register_64 (.D(Read_Data2_MEM), .en(1'b1), .clk(out_4), .Q(Read_Data2_WB));  // open: clr
  Register #(.width(1)) register_65 (.D(is_mem_inst_MEM), .en(1'b1), .clk(out_4), .Q(is_mem_inst_WB));  // open: clr
  Register #(.width(32)) register_66 (.D(ALU_Result_MEM), .en(1'b1), .clk(out_4), .Q(ALU_Result_WB));  // open: clr
  Register #(.width(2)) register_67 (.D(MEMW_Sel_MEM), .en(1'b1), .clk(out_4), .Q(MEMW_Sel_WB));  // open: clr
  Register #(.width(1)) register_68 (.D(hit_MEM), .en(1'b1), .clk(out_4), .Q(hit_WB));  // open: clr
  Register #(.width(32)) register_69 (.D(MemReadData_MEM), .en(1'b1), .clk(out_4), .Q(MemReadData_WB));  // open: clr

  // Other names for the same wires on the sheet: J_addr[5:0] = Func_IF; SHA_IF[4:0] = J_addr[10:6];
  //   rd_IF[4:0] = J_addr[15:11]; rt_IF[4:0] = J_addr[20:16]; rs_IF[4:0] = J_addr[25:21]; hit = out_7;
  //   is_mem_inst = out_3; PC[31:28] = J_value[31:28]; Main_Clock = out_4; main_mem_read_data[31:0] = out_1;
  //   MemReadData[31:0] = out_2; opcode[5:0] = out_6; reading_from_mem = out_8; Secondary_Clock = out_5

  // Notes on the sheet:
  //   Clock
  //   PC Update
  //   PC Logic
  //   Next
  //   Jump
  //   Clk_Check
  //   Cache-memory
  //   Test_Outs
  //   is_bit_valid
endmodule
