// Logisim project l1_cache.circ as structural Verilog: 1 circuit, main circuit Cache
module Cache (
  input  [31:0] memWriteData,
  input  [31:0] memAddress,
  input  clk,
  input  [3:0] write_mask,
  input  [7:0] miss_counter_state,
  input  [31:0] main_mem_read_data,
  output hit
);

  wire and_1_out, and_3_out, block1_hit, comparator_1_eq, comparator_2_eq, LRU_Update0, LRU_Update1,
       LRU_Update2, LRU_Update3, multiplexer_3_out, multiplexer_5_out, multiplexer_6_out, multiplexer_8_out,
       not_1_out, not_2_out, or_2_out, pla_1_out, S0B0LRU, S0B0V, S0B1LRU, S0B1V, S1B0LRU, S1B0V, S1B1LRU,
       S1B1V, S2B0LRU, S2B0V, S2B1LRU, S2B1V, S3B0LRU, S3B0V, S3B1LRU, S3B1V, WE0, WE0_VT, WE1, WE1_VT, WE2,
       WE2_VT, WE3, WE3_VT, WE4, WE4_VT, WE5, WE5_VT, WE6, WE6_VT, WE7, WE7_VT, WE8, WE9, WE10, WE11, WE12,
       WE13, WE14, WE15, WE16, WE17, WE18, WE19, WE20, WE21, WE22, WE23, WE24, WE25, WE26, WE27, WE28, WE29,
       WE30, WE31;
  wire [0:0] multiplexer_7_out;
  wire [1:0] multiplexer_10_out;
  wire [2:0] counter_w_sel_out;
  wire [2:2] multiplexer_9_out;
  wire [27:0] multiplexer_2_out, multiplexer_4_out, S0B0Tag, S0B1Tag, S1B0Tag, S1B1Tag, S2B0Tag, S2B1Tag,
       S3B0Tag, S3B1Tag;
  wire [31:0] multiplexer_11_out, multiplexer_12_out, multiplexer_13_out, multiplexer_14_out,
       multiplexer_15_out, multiplexer_16_out, multiplexer_17_out, multiplexer_18_out, multiplexer_19_out,
       multiplexer_20_out, multiplexer_21_out, multiplexer_22_out, multiplexer_23_out, register_25_q,
       register_26_q, register_27_q, register_28_q, register_29_q, register_30_q, register_31_q,
       register_32_q, register_33_q, register_34_q, register_35_q, register_36_q, register_37_q,
       register_38_q, register_39_q, register_40_q, register_41_q, register_42_q, register_43_q,
       register_44_q, register_45_q, register_46_q, register_47_q, register_48_q, register_49_q,
       register_50_q, register_51_q, register_52_q, register_53_q, register_54_q, register_55_q,
       register_56_q, write_data;

  not not_1 (not_1_out, block1_hit);
  Decoder #(.select(2)) decoder_1 (
    .out0(LRU_Update0), .out1(LRU_Update1), .out2(LRU_Update2), .out3(LRU_Update3), .sel(memAddress[3:2]),
    .en(hit));
  Register #(.width(1)) register_1 (.D(block1_hit), .en(LRU_Update0), .clk(clk), .Q(S0B0LRU));  // open: clr
  Register #(.width(1)) register_2 (.D(not_1_out), .en(LRU_Update0), .clk(clk), .Q(S0B1LRU));  // open: clr
  Register #(.width(1)) register_3 (.D(block1_hit), .en(LRU_Update1), .clk(clk), .Q(S1B0LRU));  // open: clr
  Register #(.width(1)) register_4 (.D(not_1_out), .en(LRU_Update1), .clk(clk), .Q(S1B1LRU));  // open: clr
  Register #(.width(1)) register_5 (.D(block1_hit), .en(LRU_Update2), .clk(clk), .Q(S2B0LRU));  // open: clr
  Register #(.width(1)) register_6 (.D(not_1_out), .en(LRU_Update2), .clk(clk), .Q(S2B1LRU));  // open: clr
  Register #(.width(1)) register_7 (.D(block1_hit), .en(LRU_Update2), .clk(clk), .Q(S3B0LRU));  // open: clr
  Register #(.width(1)) register_8 (.D(not_1_out), .en(LRU_Update2), .clk(clk), .Q(S3B1LRU));  // open: clr
  Multiplexer #(.width(32)) multiplexer_1 (.in0(main_mem_read_data), .in1(memWriteData), .out(write_data), .sel(hit));
  Register #(.width(1)) register_9 (.D(1'b1), .en(WE0_VT), .clk(clk), .Q(S0B0V));  // open: clr
  Register #(.width(1)) register_10 (.D(1'b1), .en(WE1_VT), .clk(clk), .Q(S0B1V));  // open: clr
  Register #(.width(1)) register_11 (.D(1'b1), .en(WE2_VT), .clk(clk), .Q(S1B0V));  // open: clr
  Register #(.width(1)) register_12 (.D(1'b1), .en(WE3_VT), .clk(clk), .Q(S1B1V));  // open: clr
  Register #(.width(1)) register_13 (.D(1'b1), .en(WE4_VT), .clk(clk), .Q(S2B0V));  // open: clr
  Register #(.width(1)) register_14 (.D(1'b1), .en(WE5_VT), .clk(clk), .Q(S2B1V));  // open: clr
  Register #(.width(1)) register_15 (.D(1'b1), .en(WE6_VT), .clk(clk), .Q(S3B0V));  // open: clr
  Register #(.width(1)) register_16 (.D(1'b1), .en(WE6_VT), .clk(clk), .Q(S3B1V));  // open: clr
  Multiplexer #(.select(2), .width(28)) multiplexer_2 (
    .in0(S0B0Tag), .in1(S1B0Tag), .in2(S2B0Tag), .in3(S3B0Tag), .out(multiplexer_2_out), .sel(memAddress[3:2]));
  Multiplexer #(.select(2)) multiplexer_3 (
    .in0(S0B0V), .in1(S1B0V), .in2(S2B0V), .in3(S3B0V), .out(multiplexer_3_out), .sel(memAddress[3:2]));
  Multiplexer #(.select(2), .width(28)) multiplexer_4 (
    .in0(S0B1Tag), .in1(S1B1Tag), .in2(S2B1Tag), .in3(S3B1Tag), .out(multiplexer_4_out), .sel(memAddress[3:2]));
  Multiplexer #(.select(2)) multiplexer_5 (
    .in0(S0B1V), .in1(S1B1V), .in2(S2B1V), .in3(S3B1V), .out(multiplexer_5_out), .sel(memAddress[3:2]));
  Register #(.width(28)) register_17 (.D(memAddress[31:4]), .en(WE0_VT), .clk(clk), .Q(S0B0Tag));  // open: clr
  Register #(.width(28)) register_18 (.D(memAddress[31:4]), .en(WE1_VT), .clk(clk), .Q(S0B1Tag));  // open: clr
  Register #(.width(28)) register_19 (.D(memAddress[31:4]), .en(WE2_VT), .clk(clk), .Q(S1B0Tag));  // open: clr
  Register #(.width(28)) register_20 (.D(memAddress[31:4]), .en(WE3_VT), .clk(clk), .Q(S1B1Tag));  // open: clr
  Comparator #(.width(28)) comparator_1 (
    .a(memAddress[31:4]), .b(multiplexer_2_out), .eq(comparator_1_eq));  // open: gt, lt
  Comparator #(.width(28)) comparator_2 (
    .a(memAddress[31:4]), .b(multiplexer_4_out), .eq(comparator_2_eq));  // open: gt, lt
  Register #(.width(28)) register_21 (.D(memAddress[31:4]), .en(WE4_VT), .clk(clk), .Q(S2B0Tag));  // open: clr
  Register #(.width(28)) register_22 (.D(memAddress[31:4]), .en(WE5_VT), .clk(clk), .Q(S2B1Tag));  // open: clr
  Register #(.width(28)) register_23 (.D(memAddress[31:4]), .en(WE6_VT), .clk(clk), .Q(S3B0Tag));  // open: clr
  Register #(.width(28)) register_24 (.D(memAddress[31:4]), .en(WE6_VT), .clk(clk), .Q(S3B1Tag));  // open: clr
  and and_1 (and_1_out, comparator_1_eq, multiplexer_3_out);
  and and_2 (block1_hit, comparator_2_eq, multiplexer_5_out);
  Multiplexer #(.select(2)) multiplexer_6 (
    .in0(S0B1LRU), .in1(S1B1LRU), .in2(S2B1LRU), .in3(S3B1LRU), .out(multiplexer_6_out), .sel(memAddress[3:2]));
  Multiplexer multiplexer_7 (.in0(block1_hit), .in1(multiplexer_6_out), .out(multiplexer_7_out[0]), .sel(hit));
  PLA #(.in_width(8), .out_width(3), .\table ("00001010 100 # w0_fetch\n00001011 101 # w1_fetch\n00001100 110 # w2_fetch\n00001101 111 # w3_fetch")) counter_w_sel (
    .in(miss_counter_state), .out(counter_w_sel_out));
  Register #(.width(32)) register_25 (.D(write_data), .en(WE3), .clk(clk), .Q(register_25_q));  // open: clr
  Register #(.width(32)) register_26 (.D(write_data), .en(WE7), .clk(clk), .Q(register_26_q));  // open: clr
  Register #(.width(32)) register_27 (.D(write_data), .en(WE11), .clk(clk), .Q(register_27_q));  // open: clr
  Register #(.width(32)) register_28 (.D(write_data), .en(WE15), .clk(clk), .Q(register_28_q));  // open: clr
  Register #(.width(32)) register_29 (.D(write_data), .en(WE19), .clk(clk), .Q(register_29_q));  // open: clr
  Register #(.width(32)) register_30 (.D(write_data), .en(WE23), .clk(clk), .Q(register_30_q));  // open: clr
  Register #(.width(32)) register_31 (.D(write_data), .en(WE27), .clk(clk), .Q(register_31_q));  // open: clr
  Register #(.width(32)) register_32 (.D(write_data), .en(WE31), .clk(clk), .Q(register_32_q));  // open: clr
  PLA #(.in_width(8), .out_width(1), .\table ("00001110 1 # update_tag_valid")) pla_1 (
    .in(miss_counter_state), .out(pla_1_out));
  Register #(.width(32)) register_33 (.D(write_data), .en(WE2), .clk(clk), .Q(register_33_q));  // open: clr
  Register #(.width(32)) register_34 (.D(write_data), .en(WE6), .clk(clk), .Q(register_34_q));  // open: clr
  Register #(.width(32)) register_35 (.D(write_data), .en(WE10), .clk(clk), .Q(register_35_q));  // open: clr
  Register #(.width(32)) register_36 (.D(write_data), .en(WE14), .clk(clk), .Q(register_36_q));  // open: clr
  Register #(.width(32)) register_37 (.D(write_data), .en(WE18), .clk(clk), .Q(register_37_q));  // open: clr
  Register #(.width(32)) register_38 (.D(write_data), .en(WE22), .clk(clk), .Q(register_38_q));  // open: clr
  Register #(.width(32)) register_39 (.D(write_data), .en(WE26), .clk(clk), .Q(register_39_q));  // open: clr
  Register #(.width(32)) register_40 (.D(write_data), .en(WE30), .clk(clk), .Q(register_40_q));  // open: clr
  or or_1 (hit, and_1_out, block1_hit);
  Multiplexer #(.select(2)) multiplexer_8 (
    .in0(S0B1LRU), .in1(S1B1LRU), .in2(S2B1LRU), .in3(S3B1LRU), .out(multiplexer_8_out), .sel(memAddress[3:2]));
  Decoder #(.select(3)) decoder_2 (
    .out0(WE0_VT), .out1(WE1_VT), .out2(WE2_VT), .out3(WE3_VT), .out4(WE4_VT), .out5(WE5_VT), .out6(WE6_VT),
    .out7(WE7_VT), .sel({memAddress[3:2], multiplexer_7_out[0]}), .en(pla_1_out));
  Multiplexer multiplexer_9 (.in0(block1_hit), .in1(multiplexer_8_out), .out(multiplexer_9_out[2]), .sel(hit));
  Register #(.width(32)) register_41 (.D(write_data), .en(WE1), .clk(clk), .Q(register_41_q));  // open: clr
  Register #(.width(32)) register_42 (.D(write_data), .en(WE5), .clk(clk), .Q(register_42_q));  // open: clr
  Register #(.width(32)) register_43 (.D(write_data), .en(WE9), .clk(clk), .Q(register_43_q));  // open: clr
  Register #(.width(32)) register_44 (.D(write_data), .en(WE13), .clk(clk), .Q(register_44_q));  // open: clr
  Register #(.width(32)) register_45 (.D(write_data), .en(WE17), .clk(clk), .Q(register_45_q));  // open: clr
  Register #(.width(32)) register_46 (.D(write_data), .en(WE21), .clk(clk), .Q(register_46_q));  // open: clr
  Register #(.width(32)) register_47 (.D(write_data), .en(WE25), .clk(clk), .Q(register_47_q));  // open: clr
  Register #(.width(32)) register_48 (.D(write_data), .en(WE29), .clk(clk), .Q(register_48_q));  // open: clr
  Multiplexer #(.width(2)) multiplexer_10 (
    .in0(memAddress[1:0]), .in1(counter_w_sel_out[1:0]), .out(multiplexer_10_out), .sel(hit));
  not not_2 (not_2_out, hit);
  Register #(.width(32)) register_49 (.D(write_data), .en(WE0), .clk(clk), .Q(register_49_q));  // open: clr
  Register #(.width(32)) register_50 (.D(write_data), .en(WE4), .clk(clk), .Q(register_50_q));  // open: clr
  Register #(.width(32)) register_51 (.D(write_data), .en(WE8), .clk(clk), .Q(register_51_q));  // open: clr
  Register #(.width(32)) register_52 (.D(write_data), .en(WE12), .clk(clk), .Q(register_52_q));  // open: clr
  Register #(.width(32)) register_53 (.D(write_data), .en(WE16), .clk(clk), .Q(register_53_q));  // open: clr
  Register #(.width(32)) register_54 (.D(write_data), .en(WE20), .clk(clk), .Q(register_54_q));  // open: clr
  Register #(.width(32)) register_55 (.D(write_data), .en(WE24), .clk(clk), .Q(register_55_q));  // open: clr
  Register #(.width(32)) register_56 (.D(write_data), .en(WE28), .clk(clk), .Q(register_56_q));  // open: clr
  Decoder #(.select(5)) decoder_3 (
    .out0(WE0), .out1(WE1), .out2(WE2), .out3(WE3), .out4(WE4), .out5(WE5), .out6(WE6), .out7(WE7),
    .out8(WE8), .out9(WE9), .out10(WE10), .out11(WE11), .out12(WE12), .out13(WE13), .out14(WE14),
    .out15(WE15), .out16(WE16), .out17(WE17), .out18(WE18), .out19(WE19), .out20(WE20), .out21(WE21),
    .out22(WE22), .out23(WE23), .out24(WE24), .out25(WE25), .out26(WE26), .out27(WE27), .out28(WE28),
    .out29(WE29), .out30(WE30), .out31(WE31),
    .sel({memAddress[3:2], multiplexer_9_out[2], multiplexer_10_out}), .en(or_2_out));
  or or_2 (or_2_out, write_mask[0], and_3_out);
  and and_3 (and_3_out, not_2_out, counter_w_sel_out[2]);
  Multiplexer #(.select(2), .width(32)) multiplexer_11 (
    .in0(register_49_q), .in1(register_41_q), .in2(register_33_q), .in3(register_25_q),
    .out(multiplexer_11_out), .sel(memAddress[1:0]));
  Multiplexer #(.select(2), .width(32)) multiplexer_12 (
    .in0(register_50_q), .in1(register_42_q), .in2(register_34_q), .in3(register_26_q),
    .out(multiplexer_12_out), .sel(memAddress[1:0]));
  Multiplexer #(.select(2), .width(32)) multiplexer_13 (
    .in0(register_51_q), .in1(register_43_q), .in2(register_35_q), .in3(register_27_q),
    .out(multiplexer_13_out), .sel(memAddress[1:0]));
  Multiplexer #(.select(2), .width(32)) multiplexer_14 (
    .in0(register_52_q), .in1(register_44_q), .in2(register_36_q), .in3(register_28_q),
    .out(multiplexer_14_out), .sel(memAddress[1:0]));
  Multiplexer #(.select(2), .width(32)) multiplexer_15 (
    .in0(register_53_q), .in1(register_45_q), .in2(register_37_q), .in3(register_29_q),
    .out(multiplexer_15_out), .sel(memAddress[1:0]));
  Multiplexer #(.select(2), .width(32)) multiplexer_16 (
    .in0(register_54_q), .in1(register_46_q), .in2(register_38_q), .in3(register_30_q),
    .out(multiplexer_16_out), .sel(memAddress[1:0]));
  Multiplexer #(.select(2), .width(32)) multiplexer_17 (
    .in0(register_55_q), .in1(register_47_q), .in2(register_39_q), .in3(register_31_q),
    .out(multiplexer_17_out), .sel(memAddress[1:0]));
  Multiplexer #(.select(2), .width(32)) multiplexer_18 (
    .in0(register_56_q), .in1(register_48_q), .in2(register_40_q), .in3(register_32_q),
    .out(multiplexer_18_out), .sel(memAddress[1:0]));
  Multiplexer #(.width(32)) multiplexer_19 (
    .in0(multiplexer_11_out), .in1(multiplexer_12_out), .out(multiplexer_19_out), .sel(block1_hit));
  Multiplexer #(.width(32)) multiplexer_20 (
    .in0(multiplexer_13_out), .in1(multiplexer_14_out), .out(multiplexer_20_out), .sel(block1_hit));
  Multiplexer #(.width(32)) multiplexer_21 (
    .in0(multiplexer_15_out), .in1(multiplexer_16_out), .out(multiplexer_21_out), .sel(block1_hit));
  Multiplexer #(.width(32)) multiplexer_22 (
    .in0(multiplexer_17_out), .in1(multiplexer_18_out), .out(multiplexer_22_out), .sel(block1_hit));
  Multiplexer #(.select(2), .width(32)) multiplexer_23 (
    .in0(multiplexer_19_out), .in1(multiplexer_20_out), .in2(multiplexer_21_out), .in3(multiplexer_22_out),
    .out(multiplexer_23_out), .sel(memAddress[3:2]));

  // Other names for the same wires on the sheet: set[1:0] = memAddress[3:2]; counter_state[7:0] = miss_counter_state;
  //   mem_read_data[31:0] = main_mem_read_data; word[1:0] = memAddress[1:0]; tag[27:0] = memAddress[31:4];
  //   WE = write_mask[0]

  // Notes on the sheet:
  //   Set 0
  //   Set 1
  //   Set 2
  //   Set 3
  //   data fetched from main memory
  //   write_enable_select_logic
  //   maybe require edit
endmodule
