// Logisim project alu_test.circ as structural Verilog: 1 circuit, main circuit alu_test
module alu_test (
  input  [31:0] in1,
  input  [31:0] in2,
  input  [5:0] func,
  input  [5:0] opcode,
  output zero,
  output [31:0] Res
);

  wire [4:0] alu_control_unit_1_alu_control_bits;

  alu_control_unit alu_control_unit_1 (
    .func(func), .opcode(opcode), .ALU_control_bits(alu_control_unit_1_alu_control_bits));
  ALU alu_1 (
    .Input1(in1), .Input2(in2), .op(alu_control_unit_1_alu_control_bits), .Zero(zero), .Result(Res));  // open: SHA
endmodule
